// Logisim project ex1.circ as structural Verilog: 1 circuit, main circuit main
module main (
  input  n2,
  input  n1,
  input  n0
);

  wire and_1_out, and_2_out, not_1_out, not_2_out, not_3_out, or_1_out, or_2_out;

  not not_1 (not_1_out, n2);
  not not_2 (not_2_out, n1);
  not not_3 (not_3_out, n0);
  and and_1 (and_1_out, n2, n1);
  and and_2 (and_2_out, n2, n0);
  or or_1 (or_1_out, not_1_out, not_2_out, not_3_out);
  or or_2 (or_2_out, and_1_out, and_2_out);
  // RGBLED rgbled_1: pin names not known; wires that end beside it: or_2_out, or_1_out, 1'b0

  // Notes on the sheet:
  //   n2: initial=0x1
endmodule
