// Logisim project ex2.circ as structural Verilog: 1 circuit, main circuit main
module main (
  input  n3,
  input  n2,
  input  n1,
  input  n0
);

  wire A_out, and_1_out, B_out, C_out, D_out, E_out, F_out, G_out, n1n0_out, n1nn0_out, n2n0_out, n2nn0_out,
       n2nn1_out, nn1nn0_out, nn2n1_out, nn2nn0_out, not_1_out, not_2_out, not_3_out;

  not not_1 (not_1_out, n2);
  not not_2 (not_2_out, n1);
  not not_3 (not_3_out, n0);
  and n2n0 (n2n0_out, n2, n0);
  and nn2nn0 (nn2nn0_out, not_1_out, not_3_out);
  and nn1nn0 (nn1nn0_out, not_2_out, not_3_out);
  and n1n0 (n1n0_out, n1, n0);
  and n2nn0 (n2nn0_out, n2, not_3_out);
  and n1nn0 (n1nn0_out, n1, not_3_out);
  and nn2n1 (nn2n1_out, not_1_out, n1);
  and and_1 (and_1_out, n2, not_2_out, n0);
  and n2nn1 (n2nn1_out, n2, not_2_out);
  or B (B_out, nn1nn0_out, not_1_out, n1n0_out);
  or C (C_out, n2, not_2_out, n0);
  or A (A_out, n1, n3, n2n0_out, nn2nn0_out);
  or E (E_out, nn2nn0_out, n1nn0_out);
  or D (D_out, nn2nn0_out, n1nn0_out, n3, nn2n1_out, and_1_out);
  or F (F_out, n2nn0_out, n3, n2nn1_out, nn1nn0_out);
  or G (G_out, n2nn0_out, nn2n1_out, n3, n2nn1_out);
  _7_Segment_Display u_7_segment_display_1 (
    .g(G_out), .f(F_out), .a(A_out), .b(B_out), .e(E_out), .d(D_out), .c(C_out), .dp(1'b1));
endmodule
