// Logisim project ex3_MUX8.circ as structural Verilog: 2 circuits, main circuit main
module main (
  input  E0_V1,
  input  E1_V1,
  input  E2_V1,
  input  E3_V1,
  input  C0_V1,
  input  C1_V1,
  input  E4_V1,
  input  E5_V1,
  input  E6_V1,
  input  C2_V1,
  input  E7_V1,
  input  C0_V2,
  input  E0_V2,
  input  E1_V2,
  input  E2_V2,
  input  E3_V2,
  input  E4_V2,
  input  E5_V2,
  input  E6_V3,
  input  E7_V3,
  input  C1_V2,
  input  C2_V2,
  output S_V1,
  output S_V2
);

  wire multiplexer_1_out, multiplexer_2_out, multiplexer_3_out, multiplexer_4_out, mux4_1_s, mux4_2_s;

  Multiplexer multiplexer_1 (.in0(E0_V2), .in1(E1_V2), .out(multiplexer_1_out), .sel(C0_V2));
  Multiplexer multiplexer_2 (.in0(E2_V2), .in1(E3_V2), .out(multiplexer_2_out), .sel(C0_V2));
  Multiplexer multiplexer_3 (.in0(E4_V2), .in1(E5_V2), .out(multiplexer_3_out), .sel(C0_V2));
  Multiplexer multiplexer_4 (.in0(E6_V3), .in1(E7_V3), .out(multiplexer_4_out), .sel(C0_V2));
  MUX4 mux4_1 (.E0(E0_V1), .E1(E1_V1), .C0(C0_V1), .E2(E2_V1), .C1(C1_V1), .E3(E3_V1), .S(mux4_1_s));
  MUX4 mux4_2 (.E0(E4_V1), .E1(E5_V1), .C0(C0_V1), .E2(E6_V1), .C1(C1_V1), .E3(E7_V1), .S(mux4_2_s));
  Multiplexer multiplexer_5 (.in0(mux4_1_s), .in1(mux4_2_s), .out(S_V1), .sel(C2_V1));
  MUX4 mux4_3 (
    .E0(multiplexer_1_out), .E1(multiplexer_2_out), .C0(C1_V2), .E2(multiplexer_3_out), .C1(C2_V2),
    .E3(multiplexer_4_out), .S(S_V2));
endmodule

module MUX4 (
  input  E0,
  input  E1,
  input  C0,
  input  E2,
  input  C1,
  input  E3,
  output S
);

  wire multiplexer_1_out, multiplexer_2_out;

  Multiplexer multiplexer_1 (.in0(E0), .in1(E1), .out(multiplexer_1_out), .sel(C0));
  Multiplexer multiplexer_2 (.in0(E2), .in1(E3), .out(multiplexer_2_out), .sel(C0));
  Multiplexer multiplexer_3 (.in0(multiplexer_1_out), .in1(multiplexer_2_out), .out(S), .sel(C1));
endmodule
