// Logisim project ex4.circ as structural Verilog: 5 circuits, main circuit main
module main (
  input  [3:0] A,
  input  [3:0] B,
  input  [1:0] C_in,
  output C,
  output [3:0] S,
  output Z,
  output N
);

  wire addsoustract_1_rs, not_1_out, or_1_out;
  wire [3:0] addsoustract_1_s, bitabit_1_s, transfere_1_s;

  not not_1 (not_1_out, C_in[1]);
  AddSoustract addsoustract_1 (.A(A), .B(B), .K(C_in[0]), .Rs(addsoustract_1_rs), .S(addsoustract_1_s));
  bitabit bitabit_1 (.A(A), .B(B), .S(bitabit_1_s));
  transfere transfere_1 (.B(B), .S(transfere_1_s));
  and and_1 (C, not_1_out, addsoustract_1_rs);
  Multiplexer #(.select(2), .width(4)) multiplexer_1 (
    .in0(addsoustract_1_s), .in1(addsoustract_1_s), .in2(bitabit_1_s), .in3(transfere_1_s),
    .out({N, S[2:0]}), .sel(C_in));
  or or_1 (or_1_out, S[0], S[1], S[2], N);
  not not_2 (Z, or_1_out);

  assign S[3] = N;
endmodule

module Full_adder (
  input  E1,
  input  E0,
  input  Re,
  output S,
  output Rs
);

  wire and_1_out, and_2_out, xor_1_out;

  xor xor_1 (xor_1_out, E1, E0);
  and and_1 (and_1_out, E1, E0);
  xor xor_2 (S, xor_1_out, Re);
  and and_2 (and_2_out, xor_1_out, Re);
  or or_1 (Rs, and_2_out, and_1_out);
endmodule

module AddSoustract (
  input  [3:0] A,
  input  [3:0] B,
  input  K,
  output Rs,
  output [3:0] S
);

  wire full_adder_2_rs, full_adder_3_rs, full_adder_4_rs, xor_1_out, xor_2_out, xor_3_out, xor_4_out;

  xor xor_1 (xor_1_out, B[3], K);
  Full_adder full_adder_1 (.E1(A[3]), .E0(xor_1_out), .Re(full_adder_2_rs), .S(S[3]), .Rs(Rs));
  xor xor_2 (xor_2_out, B[2], K);
  xor xor_3 (xor_3_out, B[1], K);
  Full_adder full_adder_2 (.E1(A[2]), .E0(xor_2_out), .Re(full_adder_3_rs), .S(S[2]), .Rs(full_adder_2_rs));
  Full_adder full_adder_3 (.E1(A[1]), .E0(xor_3_out), .Re(full_adder_4_rs), .S(S[1]), .Rs(full_adder_3_rs));
  xor xor_4 (xor_4_out, B[0], K);
  Full_adder full_adder_4 (.E1(A[0]), .E0(xor_4_out), .Re(K), .S(S[0]), .Rs(full_adder_4_rs));
endmodule

module bitabit (
  input  [3:0] A,
  input  [3:0] B,
  output [3:0] S
);

  and and_1 (S[3], B[3], A[3]);
  and and_2 (S[2], B[2], A[2]);
  and and_3 (S[1], B[1], A[1]);
  and and_4 (S[0], B[0], A[0]);
endmodule

module transfere (
  input  [3:0] B,
  output [3:0] S
);


  assign S = B;
endmodule
