// Logisim project ex5.circ as structural Verilog: 3 circuits, main circuit main
module main (
  input  [3:0] A,
  input  [3:0] B,
  output [7:0] out_3
);

  wire mul1_2_rs, mul1_2_s, mul1_3_rs, mul1_4_rs, mul1_4_s, mul1_5_rs, mul1_5_s, mul1_6_rs, mul1_7_rs,
       mul1_7_s, mul1_8_rs, mul1_8_s, mul1_9_rs, mul1_9_s, mul1_10_rs, mul1_11_rs, mul1_11_s, mul1_12_rs,
       mul1_12_s, mul1_13_rs, mul1_14_rs, mul1_14_s, mul1_15_rs, mul1_16_rs;

  MUL1 mul1_1 (.a(A[3]), .b(B[3]), .r(mul1_2_rs), .xe(mul1_3_rs), .S(out_3[6]), .Rs(out_3[7]));
  MUL1 mul1_2 (.a(A[2]), .b(B[3]), .r(mul1_4_rs), .xe(mul1_5_rs), .S(mul1_2_s), .Rs(mul1_2_rs));
  MUL1 mul1_3 (.a(A[3]), .b(B[2]), .r(mul1_2_s), .xe(mul1_6_rs), .S(out_3[5]), .Rs(mul1_3_rs));
  MUL1 mul1_4 (.a(A[1]), .b(B[3]), .r(mul1_7_rs), .xe(mul1_8_rs), .S(mul1_4_s), .Rs(mul1_4_rs));
  MUL1 mul1_5 (.a(A[2]), .b(B[2]), .r(mul1_4_s), .xe(mul1_9_rs), .S(mul1_5_s), .Rs(mul1_5_rs));
  MUL1 mul1_6 (.a(A[3]), .b(B[1]), .r(mul1_5_s), .xe(mul1_10_rs), .S(out_3[4]), .Rs(mul1_6_rs));
  MUL1 mul1_7 (.a(A[0]), .b(B[3]), .xe(mul1_11_rs), .S(mul1_7_s), .Rs(mul1_7_rs));  // open: r
  MUL1 mul1_8 (.a(A[1]), .b(B[2]), .r(mul1_7_s), .xe(mul1_12_rs), .S(mul1_8_s), .Rs(mul1_8_rs));
  MUL1 mul1_9 (.a(A[2]), .b(B[1]), .r(mul1_8_s), .xe(mul1_13_rs), .S(mul1_9_s), .Rs(mul1_9_rs));
  MUL1 mul1_10 (.a(A[3]), .b(B[0]), .r(mul1_9_s), .S(out_3[3]), .Rs(mul1_10_rs));  // open: xe
  MUL1 mul1_11 (.a(A[0]), .b(B[2]), .xe(mul1_14_rs), .S(mul1_11_s), .Rs(mul1_11_rs));  // open: r
  MUL1 mul1_12 (.a(A[1]), .b(B[1]), .r(mul1_11_s), .xe(mul1_15_rs), .S(mul1_12_s), .Rs(mul1_12_rs));
  MUL1 mul1_13 (.a(A[2]), .b(B[0]), .r(mul1_12_s), .S(out_3[2]), .Rs(mul1_13_rs));  // open: xe
  MUL1 mul1_14 (.a(A[0]), .b(B[1]), .xe(mul1_16_rs), .S(mul1_14_s), .Rs(mul1_14_rs));  // open: r
  MUL1 mul1_15 (.a(A[1]), .b(B[0]), .r(mul1_14_s), .S(out_3[1]), .Rs(mul1_15_rs));  // open: xe
  MUL1 mul1_16 (.a(A[0]), .b(B[0]), .S(out_3[0]), .Rs(mul1_16_rs));  // open: r, xe
endmodule

module FullAdder (
  input  ab,
  input  r,
  input  xe,
  output S,
  output Rs
);

  wire and_1_out, and_2_out, xor_1_out;

  xor xor_1 (xor_1_out, ab, r);
  and and_1 (and_1_out, ab, r);
  xor xor_2 (S, xor_1_out, xe);
  and and_2 (and_2_out, xor_1_out, xe);
  or or_1 (Rs, and_2_out, and_1_out);
endmodule

module MUL1 (
  input  a,
  input  b,
  input  r,
  input  xe,
  output S,
  output Rs
);

  wire and_1_out;

  and and_1 (and_1_out, a, b);
  FullAdder fulladder_1 (.ab(and_1_out), .r(r), .xe(xe), .S(S), .Rs(Rs));
endmodule
