// Logisim project porte.circ as structural Verilog
module main (
  input  [1:0] Cf_C0,
  input  Init
);

  wire clock_1_out;
  wire [2:0] manu_porte_1_out_4;
  wire [6:0] visu_porte_1_s;

  Clock clock_1 (.out(clock_1_out));
  manu_porte manu_porte_1 (.Cf_C0(Cf_C0), .H(clock_1_out), .init(Init), .out_4(manu_porte_1_out_4));
  visu_porte visu_porte_1 (.E(manu_porte_1_out_4), .S(visu_porte_1_s));
  // RGBLED rgbled_1: pin names not known; wires that end beside it: visu_porte_1_s[1], visu_porte_1_s[1]
  // RGBLED rgbled_2: pin names not known; wires that end beside it: visu_porte_1_s[2], visu_porte_1_s[2]
  // RGBLED rgbled_3: pin names not known; wires that end beside it: visu_porte_1_s[0], visu_porte_1_s[0]
  // RGBLED rgbled_4: pin names not known; wires that end beside it: visu_porte_1_s[3], visu_porte_1_s[3]
  // RGBLED rgbled_5: pin names not known; wires that end beside it: visu_porte_1_s[4], visu_porte_1_s[4]
  // RGBLED rgbled_6: pin names not known; wires that end beside it: visu_porte_1_s[5], visu_porte_1_s[5]
  // RGBLED rgbled_7: pin names not known; wires that end beside it: visu_porte_1_s[6], visu_porte_1_s[6]
  // RGBLED rgbled_8: pin names not known; wires that end beside it: visu_porte_1_s[6], visu_porte_1_s[6]
  // RGBLED rgbled_9: pin names not known; wires that end beside it: visu_porte_1_s[5], visu_porte_1_s[5]
  // RGBLED rgbled_10: pin names not known; wires that end beside it: visu_porte_1_s[4], visu_porte_1_s[4]
  // RGBLED rgbled_11: pin names not known; wires that end beside it: visu_porte_1_s[3], visu_porte_1_s[3]
  // RGBLED rgbled_12: pin names not known; wires that end beside it: visu_porte_1_s[2], visu_porte_1_s[2]
  // RGBLED rgbled_13: pin names not known; wires that end beside it: visu_porte_1_s[1], visu_porte_1_s[1]
  // RGBLED rgbled_14: pin names not known; wires that end beside it: visu_porte_1_s[0], visu_porte_1_s[0]
endmodule

module visu_porte (
  input  [2:0] E,
  output [6:0] S
);

  wire nE1_nE0_out, nE1nE0_out, not_2_out, not_3_out;

  not not_1 (S[3], E[2]);
  not not_2 (not_2_out, E[1]);
  not not_3 (not_3_out, E[0]);
  and nE1nE0 (nE1nE0_out, not_2_out, not_3_out);
  and nE2nE1 (S[1], not_2_out, S[3]);
  or nE1_nE0 (nE1_nE0_out, not_3_out, not_2_out);
  or nE2_nE1 (S[5], S[3], not_2_out);
  and nE2nE1nE0 (S[0], nE1nE0_out, S[3]);
  and and_1 (S[2], S[3], nE1_nE0_out);
  or or_1 (S[4], nE1nE0_out, S[3]);
  or or_2 (S[6], S[5], not_3_out);
endmodule

module manu_porte_V1 (
  input  [1:0] Cf_Co,
  input  init,
  output [2:0] out_3
);

  wire and_1_out, and_2_out, and_3_out, and_4_out, and_5_out, and_6_out, and_7_out, and_8_out, and_9_out,
       and_10_out, and_11_out, and_12_out, clock_1_out, d_ff_2_qn, d_ff_3_qn, not_1_out, not_2_out, or_1_out,
       or_2_out, or_3_out, or_4_out, or_5_out, or_6_out, or_7_out, Q1_Q0_out, Q1Q0_out, Q2_Q1_out, Q2Q1_out,
       xor_1_out;

  and and_1 (and_1_out, Cf_Co[0], and_4_out);
  and and_2 (and_2_out, Cf_Co[1], or_1_out);
  Clock clock_1 (.out(clock_1_out));
  not not_1 (not_1_out, Cf_Co[0]);
  not not_2 (not_2_out, Cf_Co[1]);
  and and_3 (and_3_out, not_1_out, not_2_out, out_3[2]);
  and and_4 (and_4_out, Q1_Q0_out, out_3[2]);
  or or_1 (or_1_out, Q1Q0_out, out_3[2]);
  and and_5 (and_5_out, out_3[2], d_ff_2_qn, d_ff_3_qn);
  and Q2Q1 (Q2Q1_out, out_3[2], out_3[1]);
  or Q2_Q1 (Q2_Q1_out, out_3[2], out_3[1]);
  D_Flip_Flop d_ff_1 (.D(or_2_out), .clk(clock_1_out), .Q(out_3[2]), .preset(init));  // open: Qn, reset
  or or_2 (or_2_out, and_2_out, and_1_out, and_3_out);
  and and_6 (and_6_out, or_3_out, Cf_Co[0]);
  and and_7 (and_7_out, Cf_Co[1], or_4_out);
  or or_3 (or_3_out, and_5_out, Q1Q0_out);
  or or_4 (or_4_out, xor_1_out, Q2Q1_out);
  and and_8 (and_8_out, not_1_out, not_2_out, out_3[1]);
  or Q1_Q0 (Q1_Q0_out, out_3[1], out_3[0]);
  and Q1Q0 (Q1Q0_out, out_3[1], out_3[0]);
  xor xor_1 (xor_1_out, out_3[1], out_3[0]);
  D_Flip_Flop d_ff_2 (.D(or_5_out), .clk(clock_1_out), .Q(out_3[1]), .Qn(d_ff_2_qn), .preset(init));  // open: reset
  or or_5 (or_5_out, and_7_out, and_6_out, and_8_out);
  and and_9 (and_9_out, Cf_Co[0], and_12_out);
  and and_10 (and_10_out, or_6_out, Cf_Co[1]);
  or or_6 (or_6_out, Q2Q1_out, d_ff_3_qn);
  and and_11 (and_11_out, not_1_out, not_2_out, out_3[0]);
  and and_12 (and_12_out, Q2_Q1_out, d_ff_3_qn);
  D_Flip_Flop d_ff_3 (.D(or_7_out), .clk(clock_1_out), .Q(out_3[0]), .Qn(d_ff_3_qn), .preset(init));  // open: reset
  or or_7 (or_7_out, and_10_out, and_9_out, and_11_out);
endmodule

module manu_porte (
  input  [1:0] Cf_C0,
  input  H,
  input  init,
  output [2:0] out_4
);

  wire and_1_out, and_2_out, d_ff_2_qn, d_ff_3_qn, multiplexer_1_out, multiplexer_2_out, multiplexer_3_out,
       or_1_out, or_2_out, or_3_out, or_4_out, or_5_out, Q1Q0_out, Q2_Q1_out, Q2Q0_out, Q2Q1_out, xor_1_out;

  or or_1 (or_1_out, Q1Q0_out, out_4[2]);
  or or_2 (or_2_out, Q2Q0_out, Q2Q1_out);
  or Q2_Q1 (Q2_Q1_out, out_4[1], out_4[2]);
  and and_1 (and_1_out, d_ff_3_qn, d_ff_2_qn, out_4[2]);
  and Q2Q0 (Q2Q0_out, out_4[0], out_4[2]);
  and Q2Q1 (Q2Q1_out, out_4[1], out_4[2]);
  Multiplexer #(.select(2)) multiplexer_1 (
    .in0(out_4[2]), .in1(or_2_out), .in2(or_1_out), .out(multiplexer_1_out), .sel(Cf_C0));  // open: in3
  D_Flip_Flop d_ff_1 (.D(multiplexer_1_out), .clk(H), .Q(out_4[2]), .preset(init));  // open: Qn, reset
  or or_3 (or_3_out, Q2Q1_out, xor_1_out);
  or or_4 (or_4_out, Q1Q0_out, and_1_out);
  xor xor_1 (xor_1_out, out_4[0], out_4[1]);
  and Q1Q0 (Q1Q0_out, out_4[0], out_4[1]);
  D_Flip_Flop d_ff_2 (.D(multiplexer_2_out), .clk(H), .Q(out_4[1]), .Qn(d_ff_2_qn), .preset(init));  // open: reset
  Multiplexer #(.select(2)) multiplexer_2 (
    .in0(out_4[1]), .in1(or_4_out), .in2(or_3_out), .out(multiplexer_2_out), .sel(Cf_C0));  // open: in3
  or or_5 (or_5_out, Q2Q1_out, d_ff_3_qn);
  and and_2 (and_2_out, Q2_Q1_out, d_ff_3_qn);
  D_Flip_Flop d_ff_3 (.D(multiplexer_3_out), .clk(H), .Q(out_4[0]), .Qn(d_ff_3_qn), .preset(init));  // open: reset
  Multiplexer #(.select(2)) multiplexer_3 (
    .in0(out_4[0]), .in1(and_2_out), .in2(or_5_out), .out(multiplexer_3_out), .sel(Cf_C0));  // open: in3
endmodule
